// Logisim project Ch7.circ as structural Verilog
module processor (
);

  wire AluInAClk, AluInBClk, AluOutClk, CarryInClk, InsRegClk, MemClk, MemInClk, MemOutClk, MemSelClk,
       OpCodeClk, ParamClk, RegAClk, RegBClk, RegCClk, RegClk, RegInClk, RegOutClk, RegSelClk, undriven;
  wire [1:0] InsRegSel, RegInpSel;
  wire [2:0] multiplexer_2_out, n3_bit_register_1_output, n3_bit_register_2_output, n3_bit_register_3_output,
       n3_bit_register_4_output;
  wire [3:0] control_logic_1_microstep;
  wire [4:0] n5_bit_register_1_output;
  wire [7:0] n8_bit_register_1_output;
  wire [15:0] carry_in_1_out, Instruction_Register_out, memory_1_data_out, multiplexer_1_out,
       n16_bit_alu_2_1_result, n16_bit_register_1_output, n16_bit_register_2_output,
       n16_bit_register_3_output, n16_bit_register_4_output, n16_bit_register_5_output,
       n16_bit_register_6_output, n16_bit_register_7_output, n16_bit_register_8_output, Registers_data_out;

  Hex_Digit_Display hex_digit_display_1 (.value(control_logic_1_microstep));  // open: dp
  Control_Logic control_logic_1 (
    .OpCodeClk(OpCodeClk), .RegAClk(RegAClk), .RegBClk(RegBClk), .RegCClk(RegCClk), .ParamClk(ParamClk),
    .InsRegClk(InsRegClk), .AluInAClk(AluInAClk), .AluInBClk(AluInBClk), .AluOutClk(AluOutClk),
    .RegClk(RegClk), .RegSelClk(RegSelClk), .RegInClk(RegInClk), .RegOutClk(RegOutClk), .MemClk(MemClk),
    .MemSelClk(MemSelClk), .MemInClk(MemInClk), .MemOutClk(MemOutClk), .CarryInClk(CarryInClk),
    .RegInpSel(RegInpSel), .InsRegSel(InsRegSel), .OpCode(n5_bit_register_1_output),
    .MicroStep(control_logic_1_microstep));
  Instruction_Register Instruction_Register (
    .In(n16_bit_register_7_output), .Out(Instruction_Register_out), .Clock(InsRegClk));  // open: Decode
  _5_bit_register u_5_bit_register_1 (
    .Input(Instruction_Register_out[15:11]), .Output(n5_bit_register_1_output), .Clock_2(OpCodeClk));  // open: Clock
  _16_bit_register u_16_bit_register_1 (
    .Clock(AluInAClk), .Input(n16_bit_register_8_output), .Output(n16_bit_register_1_output),
    .Clock_2(undriven));
  _16_bit_register u_16_bit_register_2 (
    .Clock(undriven), .Input(n16_bit_register_8_output), .Output(n16_bit_register_2_output),
    .Clock_2(AluInBClk));
  // Probe on n5_bit_register_1_output
  _3_bit_register u_3_bit_register_1 (
    .Input(Instruction_Register_out[10:8]), .Output(n3_bit_register_1_output), .Clock_2(RegAClk));  // open: Clock
  // Probe on n3_bit_register_1_output
  // Probe on n3_bit_register_2_output
  _3_bit_register u_3_bit_register_2 (
    .Input(Instruction_Register_out[7:5]), .Output(n3_bit_register_2_output), .Clock_2(RegBClk));  // open: Clock
  // Probe on n3_bit_register_3_output
  _3_bit_register u_3_bit_register_3 (
    .Input(Instruction_Register_out[4:2]), .Output(n3_bit_register_3_output), .Clock_2(RegCClk));  // open: Clock
  _16_bit_register u_16_bit_register_3 (
    .Input(n16_bit_alu_2_1_result), .Output(n16_bit_register_3_output), .Clock_2(AluOutClk));  // open: Clock
  _16_bit_alu_2 u_16_bit_alu_2_1 (
    .A(n16_bit_register_1_output), .B(n16_bit_register_2_output), .Result(n16_bit_alu_2_1_result));  // open: CarryOut_Overflow, in_1, out_6
  _8_bit_register u_8_bit_register_1 (
    .Input(Instruction_Register_out[7:0]), .Output(n8_bit_register_1_output), .Clock_2(ParamClk));  // open: Clock
  Multiplexer #(.select(2), .width(16)) multiplexer_1 (
    .in0({{8{1'b0}}, n8_bit_register_1_output}), .in1(n16_bit_register_7_output),
    .in2(n16_bit_register_3_output), .in3(carry_in_1_out), .out(multiplexer_1_out), .sel(RegInpSel), .en(1'b1));
  Carry_In carry_in_1 (.IN(n16_bit_register_8_output), .Out(carry_in_1_out), .Carry_In(CarryInClk));
  // Probe on carry_in_1_out
  _16_bit_register u_16_bit_register_4 (
    .Input(n16_bit_register_8_output), .Output(n16_bit_register_4_output), .Clock_2(MemInClk));  // open: Clock
  Multiplexer #(.select(2), .width(3)) multiplexer_2 (
    .in0(n3_bit_register_1_output), .in1(n3_bit_register_2_output), .in2(n3_bit_register_3_output),
    .in3(3'b000), .out(multiplexer_2_out), .sel(InsRegSel), .en(1'b1));
  _16_bit_register u_16_bit_register_5 (
    .Input(multiplexer_1_out), .Output(n16_bit_register_5_output), .Clock_2(RegInClk));  // open: Clock
  // Probe on n16_bit_register_8_output
  _16_bit_register u_16_bit_register_6 (
    .Clock(MemSelClk), .Input(n16_bit_register_8_output), .Output(n16_bit_register_6_output));  // open: Clock_2
  Memory memory_1 (
    .Data_In(n16_bit_register_4_output), .Data_Out(memory_1_data_out),
    .Memory_Address(n16_bit_register_6_output), .Clock(MemClk));  // open: CLEAR
  _3_bit_register u_3_bit_register_4 (
    .Input(multiplexer_2_out), .Output(n3_bit_register_4_output), .Clock(RegSelClk));  // open: Clock_2
  _16_bit_8_word_register Registers (
    .Data_In(n16_bit_register_5_output), .Clock(RegClk), .Data_Out(Registers_data_out),
    .Select_In(n3_bit_register_4_output));  // open: Select_Out
  _16_bit_register u_16_bit_register_7 (
    .Input(memory_1_data_out), .Output(n16_bit_register_7_output), .Clock_2(MemOutClk));  // open: Clock
  // Probe on multiplexer_2_out
  _16_bit_register u_16_bit_register_8 (
    .Input(Registers_data_out), .Output(n16_bit_register_8_output), .Clock_2(RegOutClk));  // open: Clock
  // Probe on n16_bit_register_8_output
endmodule

module Control_Logic (
  input  [4:0] OpCode,
  output [3:0] MicroStep,
  output MemClk,
  output MemInClk,
  output [1:0] InsRegSel,
  output RegSelClk,
  output RegOutClk,
  output MemOutClk,
  output MemSelClk,
  output CarryInClk,
  output RegInClk,
  output [1:0] RegInpSel,
  output AluInAClk,
  output AluInBClk,
  output AluOutClk,
  output RegClk,
  output InsRegClk,
  output OpCodeClk,
  output RegAClk,
  output RegBClk,
  output RegCClk,
  output ParamClk
);

  wire clock_1_out, not_1_out;
  wire [1:0] demultiplexer_1_out0;
  wire [9:0] demultiplexer_1_out6, demultiplexer_2_out0, demultiplexer_2_out1, demultiplexer_3_out0,
       demultiplexer_3_out1, demultiplexer_3_out2, demultiplexer_3_out3;

  Hex_Digit_Display hex_digit_display_1 (.value(MicroStep));  // open: dp
  Clock clock_1 (.out(clock_1_out));
  hex_counter hex_counter_1 (.Clock_in(clock_1_out), .Out(MicroStep));
  Demultiplexer #(.select(4), .enable("false")) demultiplexer_1 (
    .out0(demultiplexer_1_out0[0]), .out1(demultiplexer_1_out0[1]), .out2(CarryInClk), .out3(RegClk),
    .out4(InsRegClk), .out5(OpCodeClk), .out6(demultiplexer_1_out6[0]), .out7(demultiplexer_1_out6[1]),
    .out8(demultiplexer_1_out6[2]), .out9(demultiplexer_1_out6[3]), .out10(demultiplexer_1_out6[4]),
    .out11(demultiplexer_1_out6[5]), .out12(demultiplexer_1_out6[6]), .out13(demultiplexer_1_out6[7]),
    .out14(demultiplexer_1_out6[8]), .out15(demultiplexer_1_out6[9]), .in(1'b1), .sel(MicroStep));
  Demultiplexer #(.width(10), .disabled(0), .enable("false")) demultiplexer_2 (
    .out0({demultiplexer_2_out0[9:7], AluOutClk, AluInBClk, demultiplexer_2_out0[4:3], AluInAClk, demultiplexer_2_out0[1:0]}),
    .out1(demultiplexer_2_out1), .in(demultiplexer_1_out6), .sel(not_1_out));
  not not_1 (not_1_out, OpCode[4]);
  Demultiplexer #(.select(2), .width(10), .enable("false")) demultiplexer_3 (
    .out0(demultiplexer_3_out0), .out1(demultiplexer_3_out1), .out2(demultiplexer_3_out2),
    .out3(demultiplexer_3_out3), .in(demultiplexer_2_out1), .sel(OpCode[1:0]));
  Selector selector_1 (
    ._00(demultiplexer_2_out0[0]), ._01(demultiplexer_2_out0[3]), ._10(AluOutClk),
    ._11(demultiplexer_1_out0[0]), .X_(InsRegSel));
  or or_1 (RegOutClk, demultiplexer_1_out0[1], demultiplexer_2_out0[1], demultiplexer_2_out0[4]);
  Selector selector_2 (._10(demultiplexer_2_out0[7]), ._11(CarryInClk), .X_(RegInpSel));  // open: _00, _01
  or or_2 (RegSelClk, demultiplexer_1_out0[0], AluOutClk, demultiplexer_2_out0[3], demultiplexer_2_out0[0]);
  or or_3 (RegInClk, CarryInClk, demultiplexer_2_out0[8]);

  assign MemOutClk = CarryInClk;
  assign MemSelClk = CarryInClk;
  assign ParamClk = OpCodeClk;
  assign RegAClk = OpCodeClk;
  assign RegBClk = OpCodeClk;
  assign RegCClk = OpCodeClk;

  // Notes on the sheet:
  //   RegClk: pull=down
  //   RegOutClk: pull=down
  //   RegAClk: pull=down
  //   AluOutClk: pull=down
  //   MemInClk: pull=down
  //   AluInBClk: pull=down
  //   MemSelClk: pull=down
  //   RegInClk: pull=down
  //   MemOutClk: pull=down
  //   RegCClk: pull=down
  //   RegBClk: pull=down
  //   AluInAClk: pull=down
  //   MemClk: pull=down
  //   CarryInClk: pull=down
  //   RegSelClk: pull=down
  //   OpCodeClk: pull=down
  //   InsRegClk: pull=down
  //   ParamClk: pull=down
endmodule

// 3
module _3_bit_register (
  input  Clock,
  input  [2:0] Input,
  input  Clock_2,
  output [2:0] Output
);

  D_Flip_Flop d_ff_1 (.clk(Clock), .D(Input[0]), .Q(Output[0]));  // open: Qn, preset, en, reset
  D_Flip_Flop d_ff_2 (.clk(Clock), .D(Input[1]), .Q(Output[1]));  // open: Qn, preset, en, reset
  D_Flip_Flop d_ff_3 (.clk(Clock), .D(Input[2]), .Q(Output[2]));  // open: Qn, preset, en, reset

  assign Clock_2 = Clock;
endmodule

// 5
module _5_bit_register (
  input  Clock,
  input  [4:0] Input,
  input  Clock_2,
  output [4:0] Output
);

  D_Flip_Flop d_ff_1 (.clk(Clock), .D(Input[0]), .Q(Output[0]));  // open: Qn, preset, en, reset
  D_Flip_Flop d_ff_2 (.clk(Clock), .D(Input[1]), .Q(Output[1]));  // open: Qn, preset, en, reset
  D_Flip_Flop d_ff_3 (.clk(Clock), .D(Input[2]), .Q(Output[2]));  // open: Qn, preset, en, reset
  D_Flip_Flop d_ff_4 (.clk(Clock), .D(Input[3]), .Q(Output[3]));  // open: Qn, preset, en, reset
  D_Flip_Flop d_ff_5 (.clk(Clock), .D(Input[4]), .Q(Output[4]));  // open: Qn, preset, en, reset

  assign Clock_2 = Clock;

  // Notes on the sheet:
  //   Input: pull=down
endmodule

// 8
module _8_bit_register (
  input  Clock,
  input  [7:0] Input,
  input  Clock_2,
  output [7:0] Output
);

  D_Flip_Flop d_ff_1 (.clk(Clock), .D(Input[0]), .Q(Output[0]));  // open: Qn, preset, en, reset
  D_Flip_Flop d_ff_2 (.clk(Clock), .D(Input[1]), .Q(Output[1]));  // open: Qn, preset, en, reset
  D_Flip_Flop d_ff_3 (.clk(Clock), .D(Input[2]), .Q(Output[2]));  // open: Qn, preset, en, reset
  D_Flip_Flop d_ff_4 (.clk(Clock), .D(Input[3]), .Q(Output[3]));  // open: Qn, preset, en, reset
  D_Flip_Flop d_ff_5 (.clk(Clock), .D(Input[4]), .Q(Output[4]));  // open: Qn, preset, en, reset
  D_Flip_Flop d_ff_6 (.clk(Clock), .D(Input[5]), .Q(Output[5]));  // open: Qn, preset, en, reset
  D_Flip_Flop d_ff_7 (.clk(Clock), .D(Input[6]), .Q(Output[6]));  // open: Qn, preset, en, reset
  D_Flip_Flop d_ff_8 (.clk(Clock), .D(Input[7]), .Q(Output[7]));  // open: Qn, preset, en, reset

  assign Clock_2 = Clock;
endmodule

// 16
module _16_bit_register (
  input  Clock,
  input  [15:0] Input,
  input  Clock_2,
  output [15:0] Output
);

  D_Flip_Flop d_ff_1 (.clk(Clock), .D(Input[14]), .Q(Output[14]));  // open: Qn, preset, en, reset
  D_Flip_Flop d_ff_2 (.clk(Clock), .D(Input[6]), .Q(Output[6]));  // open: Qn, preset, en, reset
  D_Flip_Flop d_ff_3 (.clk(Clock), .D(Input[8]), .Q(Output[8]));  // open: Qn, preset, en, reset
  D_Flip_Flop d_ff_4 (.clk(Clock), .D(Input[10]), .Q(Output[10]));  // open: Qn, preset, en, reset
  D_Flip_Flop d_ff_5 (.clk(Clock), .D(Input[12]), .Q(Output[12]));  // open: Qn, preset, en, reset
  D_Flip_Flop d_ff_6 (.clk(Clock), .D(Input[13]), .Q(Output[13]));  // open: Qn, preset, en, reset
  D_Flip_Flop d_ff_7 (.clk(Clock), .D(Input[15]), .Q(Output[15]));  // open: Qn, preset, en, reset
  D_Flip_Flop d_ff_8 (.clk(Clock), .D(Input[0]), .Q(Output[0]));  // open: Qn, preset, en, reset
  D_Flip_Flop d_ff_9 (.clk(Clock), .D(Input[2]), .Q(Output[2]));  // open: Qn, preset, en, reset
  D_Flip_Flop d_ff_10 (.clk(Clock), .D(Input[4]), .Q(Output[4]));  // open: Qn, preset, en, reset
  D_Flip_Flop d_ff_11 (.clk(Clock), .D(Input[5]), .Q(Output[5]));  // open: Qn, preset, en, reset
  D_Flip_Flop d_ff_12 (.clk(Clock), .D(Input[7]), .Q(Output[7]));  // open: Qn, preset, en, reset
  D_Flip_Flop d_ff_13 (.clk(Clock), .D(Input[9]), .Q(Output[9]));  // open: Qn, preset, en, reset
  D_Flip_Flop d_ff_14 (.clk(Clock), .D(Input[11]), .Q(Output[11]));  // open: Qn, preset, en, reset
  D_Flip_Flop d_ff_15 (.clk(Clock), .D(Input[1]), .Q(Output[1]));  // open: Qn, preset, en, reset
  D_Flip_Flop d_ff_16 (.clk(Clock), .D(Input[3]), .Q(Output[3]));  // open: Qn, preset, en, reset

  assign Clock_2 = Clock;
endmodule

module Instruction_Register (
  input  Decode,
  input  [15:0] In,
  input  Clock,
  output [15:0] Out
);

  Register #(.width(16), .trigger("high")) register_1 (.D(In), .clk(Clock));  // open: en, Q, clr

  assign Out = 16'h994c;
endmodule

module Carry_In (
  input  [15:0] IN,
  input  Carry_In,
  output [15:0] Out
);

  _16_bit_adder__bundled_i_o u_16_bit_adder_bundled_i_o_1 (
    .CarryIn(Carry_In), .A(IN), .B({16{1'b0}}), .Out(Out));  // open: CarryOut

  // Notes on the sheet:
  //   Out: pull=down
endmodule

module Memory (
  input  CLEAR,
  input  [15:0] Memory_Address,
  input  [15:0] Data_In,
  input  Clock,
  output [15:0] Data_Out
);

  RAM #(.addrWidth(16), .dataWidth(16), .bus("separate")) ram_1 (
    .addr(Memory_Address), .din(Data_In), .data(Data_Out), .str(1'b1), .sel(1'b1), .clk(Clock), .ld(1'b1),
    .clr(CLEAR));

  // Notes on the sheet:
  //   Data_Out: pull=down
endmodule

module Selector (
  input  _00,
  input  _01,
  input  _10,
  input  _11,
  output [1:0] X_
);

  wire nand_1_out, nand_2_out, nand_3_out, nand_4_out, nand_5_out, nand_6_out, undriven, undriven_2,
       undriven_3;

  or or_1 (X_[1], _11, _10);
  or or_2 (X_[0], _11, _01);
  nand nand_1 (nand_1_out, undriven_3, undriven_3);
  nand nand_2 (nand_2_out, undriven_2, undriven_2);
  nand nand_3 (nand_3_out, undriven_3, undriven_3);
  nand nand_4 (nand_4_out, undriven, undriven);
  nand nand_5 (nand_5_out, nand_1_out, nand_2_out);
  nand nand_6 (nand_6_out, nand_3_out, nand_4_out);

  // Notes on the sheet:
  //   _00: pull=down
  //   _11: pull=down
  //   X_: pull=down
  //   _01: pull=down
  //   _10: pull=down
endmodule

module Counter (
);

  wire clock_1_out, clock_2_out, flipflo_1_out_1, flipflo_1_out_2, flipflo_2_out_2, flipflo_3_out_1,
       flipflo_3_out_2, nand_1_out, nand_2_out, nand_3_out, nand_4_out, nand_5_out, nand_6_out, nand_7_out,
       nand_8_out, nand_9_out, nand_10_out, nand_11_out, nand_12_out, nand_13_out, nand_14_out, nand_15_out;

  Clock clock_1 (.out(clock_1_out));
  Clock clock_2 (.out(clock_2_out));
  LED led_1 (.in(flipflo_1_out_2));
  FlipFlo flipflo_1 (.in_1(flipflo_1_out_2), .sync(clock_1_out), .out_1(flipflo_1_out_1), .out_2(flipflo_1_out_2));
  LED led_2 (.in(flipflo_3_out_2));
  FlipFlo flipflo_2 (.in_1(flipflo_2_out_2), .sync(flipflo_3_out_1), .out_2(flipflo_2_out_2));  // open: out_1
  FlipFlo flipflo_3 (.in_1(flipflo_3_out_2), .sync(flipflo_1_out_1), .out_1(flipflo_3_out_1), .out_2(flipflo_3_out_2));
  nand nand_1 (nand_1_out, nand_5_out, clock_2_out);
  nand nand_2 (nand_2_out, clock_2_out, nand_3_out);
  nand nand_3 (nand_3_out, nand_5_out, nand_5_out);
  LED led_3 (.in(flipflo_2_out_2));
  nand nand_4 (nand_4_out, nand_1_out, nand_5_out);
  nand nand_5 (nand_5_out, nand_4_out, nand_2_out);
  nand nand_6 (nand_6_out, nand_10_out, nand_4_out);
  nand nand_7 (nand_7_out, nand_4_out, nand_8_out);
  nand nand_8 (nand_8_out, nand_10_out, nand_10_out);
  nand nand_9 (nand_9_out, nand_6_out, nand_10_out);
  nand nand_10 (nand_10_out, nand_9_out, nand_7_out);
  nand nand_11 (nand_11_out, nand_15_out, nand_15_out);
  nand nand_12 (nand_12_out, nand_15_out, nand_9_out);
  nand nand_13 (nand_13_out, nand_9_out, nand_11_out);
  nand nand_14 (nand_14_out, nand_12_out, nand_15_out);
  nand nand_15 (nand_15_out, nand_14_out, nand_13_out);
endmodule

module FlipFlo (
  input  in_1,
  input  sync,
  output out_1,
  output out_2
);

  wire nand_1_out, nand_2_out, nand_3_out;

  nand nand_1 (nand_1_out, in_1, sync);
  nand nand_2 (nand_2_out, sync, nand_3_out);
  nand nand_3 (nand_3_out, in_1, in_1);
  nand nand_4 (out_1, nand_1_out, out_2);
  nand nand_5 (out_2, out_1, nand_2_out);
endmodule
